# Fritzing sketch ThirdAssignment_LisaCocchia_793569 (saved by Fritzing 0.9.3b)
breadboards: 2

parts:
  U1 = NodeMCU V1.0
  DHT22 = AM2302 DHT22 Humidity and Temperature Sensor
  Capacitive_Soil_Moisture_Sensor1 = DFRobot Capacitive Soil Moisture Sensor V1.0 [part_number=SEN0193]
  Piezo2 = Piezo Speaker - PC Mount [part_number=COM-07950]
  PIR_HC-SR502 = HC-SR501 Body Sensor Module
  R6 = PHOTOCELL [package=photocell]
  R7 = Resistor [tolerance=±5% resistance=200 package="0603 [SMD]"]
  R8 = Resistor [tolerance=±5% resistance=200 package="0603 [SMD]"]
  I2C_LCD_Display_(16x2)_1 = LCD1602-I2C
  U2 = NodeMCU V1.0
  R9 = Resistor [tolerance=±5% resistance=200 package="0603 [SMD]"]
  LED2 = smd LED [color="Yellow (595nm)" package="1206 [SMD]"]
  Solid_state_relay = Solid State High Level Relay Module [package=relay]
  WATER_PUMP = water pump/motor
  R10 = Resistor [tolerance=±5% resistance=1k package="0402 [SMD]"]
  2kΩ = Resistor [tolerance=±5% resistance=2.2k package="0402 [SMD]"]
  J1 = Basic Servo

nets:
  N1: U1.D5, Solid_state_relay.CH1
  N2: U1.D6, DHT22.DAT
  N3: U1.D7, J1.pulse
  N4: U1.A0, R10.Pin_0, 2kΩ.Pin_1
  N5: Capacitive_Soil_Moisture_Sensor1.A, R10.Pin_1
  VCC: Capacitive_Soil_Moisture_Sensor1.VCC, Solid_state_relay.DC+, Solid_state_relay.B1, J1.vcc
  GND: Capacitive_Soil_Moisture_Sensor1.GND, Solid_state_relay.DC-, WATER_PUMP.pin_1, 2kΩ.Pin_0, J1.gnd
  GND_2: Piezo2.GND, PIR_HC-SR502.GND, R8.Pin_0, I2C_LCD_Display_(16x2)_1.GND, U2.GND, R9.Pin_1
  N6: Piezo2.VCC, R7.Pin_0
  VCC_2: PIR_HC-SR502.VCC, I2C_LCD_Display_(16x2)_1.VCC, U2.Vin
  N7: PIR_HC-SR502.OUT, U2.D7
  N8: R6.P$1, R8.Pin_1, U2.3V3
  N9: R6.P$2, U2.A0
  N10: R7.Pin_1, U2.D8
  N11: I2C_LCD_Display_(16x2)_1.SDA, I2C_LCD_Display_(16x2)_1.SCL, U2.D1
  N12: U2.D6, LED2.anode
  N13: R9.Pin_0, LED2.cathode
  N14: Solid_state_relay.A1, WATER_PUMP.pin_2

custom parts:
  NodeMCU V1.0: ESP8266 based NodeMCU
  DFRobot Capacitive Soil Moisture Sensor V1.0: DFRobot Capacitive Soil Moisture Sensor V1.0 This product measures soil moisture levels by capacitive sensing, rather than resistive sensing like other types of moisture sensor. It is made of a corrosion resistant material giving it a long service life. Insert it into soil and impress your friends with the real-time soil moisture data! The product includes an on-board voltage regulator which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
  Piezo Speaker - PC Mount: This is a small 12mm round speaker that operates around the audible 2kHz range. You can use these speakers to create simple music or user interfaces. Each speaker is PTH solderable and requires an operating voltage of 3.5-5V with a mean current of 35mA max. These speakers also have a typical sound output of 95 dBA and a coil resistance of 42 ±6.3 ohms.
  HC-SR501 Body Sensor Module: Pyroelectric Infrared PIR Motion Sensor Detector Module
  LCD1602-I2C: A standard character display, usually with 2x16 characters. Comes in many colors with LCM1602 IIC attached.
  Solid State High Level Relay Module: 5V Omron solid state relay 240V 2A output with resistance fuse.
  water pump/motor: WATER PUMP BY ARDUBLOCKTR
